# Fritzing sketch PROJETO EMBARCADOS (saved by Fritzing 0.9.3b)
breadboards: 1

parts:
  LCM1602_IIC1 = LCM1602 IIC [part_number="LCM1602 IIC" chip_label="LCM1602 IIC" package="DIP (Dual Inline) [THT]"]
  U2 = LCD-16X2 [package=lcd-16x2_noholes]
  ZS-042_RTC1 = ZS-042 RTC Module
  U1 = ESP32-38PinWide [part_number=ESP32-38PinWide]
  J1 = Generic female header - 2 pins [form="♀ (female)" package=THT]
  R1 = Resistor [tolerance=±5% resistance=10 package="0603 [SMD]"]
  R2 = Resistor [tolerance=±5% resistance=10 package="0603 [SMD]"]
  C1 = Capacitor Polarized [package=cpol-radial-10uf-25v]
  R3 = Resistor [tolerance=±5% resistance=10k package="0603 [SMD]"]
  R4 = Resistor [tolerance=±5% resistance=10k package="0603 [SMD]"]

nets:
  VSS: LCM1602_IIC1.VSS, U2.VSS
  VDD: LCM1602_IIC1.VDD, U2.VDD
  N1: LCM1602_IIC1.V0, U2.VO
  N2: LCM1602_IIC1.RS, U2.RS
  N3: LCM1602_IIC1.RW, U2.R_W
  N4: LCM1602_IIC1.E, U2.E
  N5: LCM1602_IIC1.D0, U2.DB0
  N6: LCM1602_IIC1.D1, U2.DB1
  N7: LCM1602_IIC1.D2, U2.DB2
  N8: LCM1602_IIC1.D3, U2.DB3
  N9: LCM1602_IIC1.D4, U2.DB4
  N10: LCM1602_IIC1.D5, U2.DB5
  N11: LCM1602_IIC1.D6, U2.DB6
  N12: LCM1602_IIC1.D7, U2.DB7
  N13: LCM1602_IIC1.A, U2.A
  N14: LCM1602_IIC1.K, U2.K
  GND: LCM1602_IIC1.GND, ZS-042_RTC1.GND, U1.GND
  VCC: LCM1602_IIC1.VCC, ZS-042_RTC1.VCC, U1.GPIO21
  N15: U1.3.3, J1.pin2, R2.Pin_1
  N16: J1.pin1, R1.Pin_0, C1.+, R3.Pin_0, R4.Pin_1
  N17: R1.Pin_1, R2.Pin_0
  N18: C1.-, R3.Pin_1

notes:
  SMART MDE - MEDIDOR
  IFCE CAMPUS TAUÁ - TELEMÁTICA
  PROJETO SISTEMAS EMBARCADOS 2021.1
  (S, R.; C, A.; I, M.)

custom parts:
  LCM1602 IIC: I2C-Module to use a 1602 or 2004 LCD on with the wire.h libory Serial LCD Modul
  ESP32-38PinWide: Generic 38-Pin ESP32 with wide format (only access to one side of pins on a breadboard) based on Stephen Lilley's HiLetgo ESP-WROOM-32 ESP32 ESP-32S Development Board.
  Generic female header - 2 pins: Generic female header
